# Fritzing sketch Fritzing_controleur_MIDI (saved by Fritzing 0.9.3b)
perfboards: 1

parts:
  Composant1 = Arduino Mega Proto Shield (v6)  # not connected
  R1 = Slide Potentiometer [maximum_resistance=100kΩ]
  R2 = Slide Potentiometer [maximum_resistance=100kΩ]
  R3 = Slide Potentiometer [maximum_resistance=100kΩ]
  R4 = Slide Potentiometer [maximum_resistance=100kΩ]

nets:
  N1: R1.leg1, R2.leg1, R3.leg1, R4.leg1
  N2: R1.wiper, R2.wiper, R3.wiper, R4.wiper
